# Fritzing sketch ServoIncrementalPos (saved by Fritzing 0.6.3b)

parts:
  Arduino1 = Arduino
  J1 = Basic Servo

nets:
  GND: Arduino1.GND, J1.gnd
  N1: Arduino1.D6, J1.pulse
  +5V: Arduino1.+5V, J1.vcc
