# Fritzing sketch AnalogSensorAndFading (saved by Fritzing 0.6.3b)
breadboards: 1

parts:
  Arduino1 = Arduino
  LED1 = LED - 5mm [color="Red (633nm)" package="5 mm [THT]"]
  R1 = Resistor [tolerance=±5% resistance=330 package=THT]
  R2 = Basic Flex Resistor
  R3 = Resistor [tolerance=±5% resistance=10k package=THT]

nets:
  N1: Arduino1.GND, LED1.cathode, R3.Pin_0
  N2: Arduino1.D3, R1.Pin_1
  N3: Arduino1.+5V, R2.Pin_2
  N4: Arduino1.A0, R2.pin_1, R3.Pin_1
  N5: LED1.anode, R1.Pin_0
