# Fritzing sketch AnalogSensorAndMotor (saved by Fritzing 0.6.3b)
breadboards: 1

parts:
  Arduino1 = Arduino
  IC1 = H-Bridge [package=THT]
  M1 = DC Motor
  R1 = Rotary Potentiometer (Small) [maximum_resistance=100kΩ]

nets:
  GND: Arduino1.GND, IC1.GND1, IC1.GND2, IC1.GND3, IC1.GND4, R1.leg2
  N1: Arduino1.D5, IC1.1A
  N2: Arduino1.D4, IC1.2A
  N3: Arduino1.D3, IC1.1_2EN
  N4: Arduino1.+5V, IC1.VCC2, IC1.VCC1, R1.leg1
  N5: Arduino1.A0, R1.wiper
  N6: IC1.1Y, M1.pin_1
  N7: IC1.2Y, M1.pin_2
