# Fritzing sketch FiveLEDS (saved by Fritzing 0.6.3b)
breadboards: 1

parts:
  Arduino1 = Arduino
  LED1 = LED - 5mm [color="Yellow (595nm)" package="5 mm [THT]"]
  LED2 = LED - 5mm [color="Red (633nm)" package="5 mm [THT]"]
  LED3 = LED - 5mm [color="Yellow (595nm)" package="5 mm [THT]"]
  LED4 = LED - 5mm [color="Red (633nm)" package="5 mm [THT]"]
  LED5 = LED - 5mm [color="Yellow (595nm)" package="5 mm [THT]"]
  R1 = Resistor [tolerance=±5% resistance=330 package=THT]
  R2 = Resistor [tolerance=±5% resistance=330 package=THT]
  R3 = Resistor [tolerance=±5% resistance=330 package=THT]
  R4 = Resistor [tolerance=±5% resistance=330 package=THT]
  R5 = Resistor [tolerance=±5% resistance=330 package=THT]

nets:
  N1: Arduino1.GND, LED1.cathode, LED2.cathode, LED3.cathode, LED4.cathode, LED5.cathode
  N2: Arduino1.D12, R1.Pin_1
  N3: Arduino1.D11, R2.Pin_1
  N4: Arduino1.D10, R3.Pin_1
  N5: Arduino1.D9, R4.Pin_1
  N6: Arduino1.D8, R5.Pin_1
  N7: LED1.anode, R1.Pin_0
  N8: LED2.anode, R2.Pin_0
  N9: LED3.anode, R3.Pin_0
  N10: LED4.anode, R4.Pin_0
  N11: LED5.anode, R5.Pin_0
