# Fritzing sketch HBridgeAndDCMotor (saved by Fritzing 0.6.3b)
breadboards: 1

parts:
  Arduino1 = Arduino
  IC1 = H-Bridge [package=THT]
  M1 = DC Motor

nets:
  GND: Arduino1.GND, IC1.GND1, IC1.GND2, IC1.GND3, IC1.GND4
  N1: Arduino1.D5, IC1.1A
  N2: Arduino1.D4, IC1.2A
  N3: Arduino1.D3, IC1.1_2EN
  N4: Arduino1.+5V, IC1.VCC2, IC1.VCC1
  N5: IC1.1Y, M1.pin_1
  N6: IC1.2Y, M1.pin_2
